// Logisim project ripple-counter.circ as structural Verilog: 1 circuit, main circuit main
module main (
);

  wire CLOCK_out, not_1_out, not_2_out, T0_q, T1_q, T2_q;

  not not_1 (not_1_out, T1_q);
  T_Flip_Flop T2 (.clk(not_1_out), .T(1'b1), .Q(T2_q));  // open: Qn, preset, reset, en
  LED led_1 (.in(T2_q));
  T_Flip_Flop T1 (.clk(not_2_out), .T(1'b1), .Q(T1_q));  // open: Qn, preset, reset, en
  not not_2 (not_2_out, T0_q);
  Button CLOCK (.out(CLOCK_out));
  LED led_2 (.in(T1_q));
  T_Flip_Flop T0 (.clk(CLOCK_out), .T(1'b1), .Q(T0_q));  // open: Qn, preset, reset, en
  LED led_3 (.in(T0_q));
endmodule
