// Logisim project shift-register.circ as structural Verilog: 1 circuit, main circuit main
module main (
  input  INPUT
);

  wire CLOCK_out, d_ff_1_q, d_ff_2_q, d_ff_3_q, RESET_out;

  Button CLOCK (.out(CLOCK_out));
  D_Flip_Flop d_ff_1 (.clk(CLOCK_out), .D(INPUT), .Q(d_ff_1_q), .reset(RESET_out));  // open: Qn, preset, en
  Button RESET (.out(RESET_out));
  D_Flip_Flop d_ff_2 (.clk(CLOCK_out), .D(d_ff_1_q), .Q(d_ff_2_q), .reset(RESET_out));  // open: Qn, preset, en
  D_Flip_Flop d_ff_3 (.clk(CLOCK_out), .D(d_ff_2_q), .Q(d_ff_3_q), .reset(RESET_out));  // open: Qn, preset, en
  D_Flip_Flop d_ff_4 (.clk(CLOCK_out), .D(d_ff_3_q), .reset(RESET_out));  // open: Q, Qn, preset, en
endmodule
