// Logisim project synchronous-counter.circ as structural Verilog: 1 circuit, main circuit main
module main (
  output out_1,
  output out_2,
  output out_3,
  output out_4
);

  wire and_1_out, and_2_out, CLOCK_out;

  Button CLOCK (.out(CLOCK_out));
  T_Flip_Flop T3 (.clk(CLOCK_out), .T(1'b1), .Q(out_4));  // open: Qn, preset, reset, en
  T_Flip_Flop T2 (.clk(CLOCK_out), .T(out_4), .Q(out_3));  // open: Qn, preset, reset, en
  and and_1 (and_1_out, out_3, out_4);
  T_Flip_Flop T1 (.clk(CLOCK_out), .T(and_1_out), .Q(out_2));  // open: Qn, preset, reset, en
  and and_2 (and_2_out, out_2, and_1_out);
  T_Flip_Flop T0 (.clk(CLOCK_out), .T(and_2_out), .Q(out_1));  // open: Qn, preset, reset, en
endmodule
