// Logisim project ex1.circ as structural Verilog: 1 circuit, main circuit main
module main (
  input  A,
  input  B,
  output S
);

  wire nand_1_out, or_1_out;

  or or_1 (or_1_out, A, B);
  nand nand_1 (nand_1_out, B, A);
  and and_1 (S, or_1_out, nand_1_out);

  // Notes on the sheet:
  //   OU Exclusif
endmodule
