// Logisim project ex2.2.circ as structural Verilog: 4 circuits, main circuit main
module main (
  input  x1,
  input  x2,
  input  x4,
  input  x8,
  input  y1,
  input  y2,
  input  y4,
  input  y8
);
endmodule

// Add1
module add1 (
  input  A,
  input  B,
  output S,
  output Rs
);

  xor xor_1 (S, A, B);
  and and_1 (Rs, A, B);
endmodule

module add1r (
  input  A,
  input  B,
  input  Re,
  output S,
  output Rs
);

  wire and_1_out, and_2_out, and_3_out, and_4_out, and_5_out, and_6_out, and_7_out, not_1_out, not_2_out,
       not_3_out, not_4_out, not_5_out, not_6_out;

  not not_1 (not_1_out, A);
  not not_2 (not_2_out, B);
  not not_3 (not_3_out, A);
  not not_4 (not_4_out, Re);
  not not_5 (not_5_out, B);
  not not_6 (not_6_out, Re);
  and and_1 (and_1_out, A, B);
  and and_2 (and_2_out, A, Re);
  and and_3 (and_3_out, B, Re);
  and and_4 (and_4_out, not_1_out, not_2_out, Re);
  and and_5 (and_5_out, not_3_out, B, not_4_out);
  and and_6 (and_6_out, A, not_5_out, not_6_out);
  and and_7 (and_7_out, A, B, Re);
  or or_1 (Rs, and_1_out, and_2_out, and_3_out);
  or or_2 (S, and_4_out, and_5_out, and_6_out, and_7_out);
endmodule

// Add1r
module add1r2 (
  input  A,
  input  B,
  input  Re,
  output S,
  output Rs
);

  wire add1_1_rs, add1_1_s, add1_2_rs;

  add1 add1_1 (.A(A), .B(B), .S(add1_1_s), .Rs(add1_1_rs));
  add1 add1_2 (.A(add1_1_s), .B(Re), .S(S), .Rs(add1_2_rs));
  or or_1 (Rs, add1_1_rs, add1_2_rs);
endmodule
