// Logisim project basculecompter.circ as structural Verilog: 1 circuit, main circuit main
module main (
  input  e,
  output q2,
  output q1,
  output q0
);

  wire and_1_out, and_2_out, and_3_out, and_4_out, and_5_out, and_6_out, and_7_out, and_8_out, and_9_out,
       and_10_out, and_11_out, and_12_out, clock_1_out, or_1_out, or_2_out, or_3_out, or_4_out, or_5_out;

  and and_1 (and_1_out, ~q2, e, q2, q2);  // AND_Gate
  and and_2 (and_2_out, ~q1, e);  // AND_Gate
  and and_3 (and_3_out, ~e, q2);  // AND_Gate
  and and_4 (and_4_out, ~q0, e);  // AND_Gate
  and and_5 (and_5_out, ~q2, q0, q2);  // AND_Gate
  and and_6 (and_6_out, ~q2, ~e);  // AND_Gate
  and and_7 (and_7_out, ~e, q2, q2);  // AND_Gate
  and and_8 (and_8_out, ~q2, q2, e);  // AND_Gate
  or or_1 (or_1_out, and_6_out, q1, and_2_out);
  or or_2 (or_2_out, ~q0, ~e);  // OR_Gate
  or or_3 (or_3_out, and_3_out, and_4_out);
  and and_9 (and_9_out, ~e, ~q0, q1);  // AND_Gate
  or or_4 (or_4_out, and_7_out, and_9_out, and_8_out, and_5_out, and_1_out);
  and and_10 (and_10_out, or_2_out, q2, q1);
  and and_11 (and_11_out, q2, or_3_out);
  Clock clock_1 (.out(clock_1_out));
  and and_12 (and_12_out, q0, or_1_out);
  or or_5 (or_5_out, and_10_out, and_11_out);
  D_Flip_Flop D2 (.clk(clock_1_out), .D(or_4_out), .Q(q2));  // open: Qn, preset, en, reset
  D_Flip_Flop D0 (.clk(clock_1_out), .D(or_5_out), .Q(q0));  // open: Qn, preset, en, reset
  D_Flip_Flop D1 (.clk(clock_1_out), .D(and_12_out), .Q(q1));  // open: Qn, preset, en, reset
endmodule
