// Logisim project rs.circ as structural Verilog
module main (
  output out_1,
  output out_2
);
endmodule

module RS (
  input  [7:0] S,
  input  Horloge,
  input  Reset,
  output [7:0] Out
);

  S_R_Flip_Flop s_r_ff_1 (.S(S[0]), .clk(Horloge), .R(Reset), .Q(Out[0]));  // open: Qn, preset, reset, en
  S_R_Flip_Flop s_r_ff_2 (.S(S[1]), .clk(Horloge), .R(Reset), .Q(Out[1]));  // open: Qn, preset, reset, en
  S_R_Flip_Flop s_r_ff_3 (.S(S[2]), .clk(Horloge), .R(Reset), .Q(Out[2]));  // open: Qn, preset, reset, en
  S_R_Flip_Flop s_r_ff_4 (.S(S[3]), .clk(Horloge), .R(Reset), .Q(Out[3]));  // open: Qn, preset, reset, en
  S_R_Flip_Flop s_r_ff_5 (.S(S[4]), .clk(Horloge), .R(Reset), .Q(Out[4]));  // open: Qn, preset, reset, en
  S_R_Flip_Flop s_r_ff_6 (.S(S[5]), .clk(Horloge), .R(Reset), .Q(Out[5]));  // open: Qn, preset, reset, en
  S_R_Flip_Flop s_r_ff_7 (.S(S[6]), .clk(Horloge), .R(Reset), .Q(Out[6]));  // open: Qn, preset, reset, en
  S_R_Flip_Flop s_r_ff_8 (.S(S[7]), .clk(Horloge), .R(Reset), .Q(Out[7]));  // open: Qn, preset, reset, en
endmodule

module _2 (
  input  [7:0] a,
  input  [7:0] a_2,
  input  in_3,
  input  in_4,
  input  [7:0] b,
  output [7:0] out_6
);

  wire clock_1_out;
  wire [7:0] multiplexer_1_out, rs_1_out;

  Clock clock_1 (.out(clock_1_out));
  RS rs_1 (.S(a_2), .Horloge(clock_1_out), .Reset(in_3), .Out(rs_1_out));
  Multiplexer #(.width(8)) multiplexer_1 (.in0(a), .in1(rs_1_out), .out(multiplexer_1_out), .sel(in_4));  // open: en
  Adder adder_1 (.a(multiplexer_1_out), .b(b), .out(out_6));  // open: cin, cout

  // Notes on the sheet:
  //   a
  //   b
endmodule

module Ca2 (
  input  [7:0] a,
  output [7:0] out_2
);


  assign a[5:0] = {6{a[6]}};
  assign out_2[5:0] = {6{out_2[6]}};
endmodule
