// Logisim project vending-machine.circ as structural Verilog: 1 circuit, main circuit main
module main (
  input  J,
  input  I
);

  wire and_1_out, and_2_out, and_3_out, and_4_out, and_5_out, and_6_out, and_7_out, and_8_out, and_9_out,
       and_10_out, CLOCK_out, not_1_out, not_2_out, or_1_out, or_2_out, or_3_out, q0_q, q0_qn, q1_q, q1_qn,
       RESET_out;

  Clock CLOCK (.out(CLOCK_out));
  and and_1 (and_1_out, J, CLOCK_out);
  and and_2 (and_2_out, I, CLOCK_out);
  Button RESET (.out(RESET_out));
  not not_1 (not_1_out, and_1_out);
  not not_2 (not_2_out, and_2_out);
  and and_3 (and_3_out, q1_q, not_2_out);
  and and_4 (and_4_out, not_1_out, and_2_out, q0_qn, q1_qn);
  D_Flip_Flop #(.trigger("falling")) q1 (
    .clk(CLOCK_out), .D(or_1_out), .Q(q1_q), .Qn(q1_qn), .reset(RESET_out));  // open: preset, en
  or or_1 (or_1_out, and_3_out, and_4_out);
  and and_5 (and_5_out, and_2_out, and_1_out, q1_q);
  and and_6 (and_6_out, q0_q, not_2_out);
  and and_7 (and_7_out, not_1_out, q1_q, and_2_out);
  and and_8 (and_8_out, and_1_out, q1_qn, and_2_out, q0_qn);
  or or_2 (or_2_out, and_6_out, and_7_out, and_8_out);
  D_Flip_Flop #(.trigger("falling")) q0 (
    .clk(CLOCK_out), .D(or_2_out), .Q(q0_q), .Qn(q0_qn), .reset(RESET_out));  // open: preset, en
  and and_9 (and_9_out, q0_q, and_2_out);
  or or_3 (or_3_out, and_5_out, and_9_out);
  and and_10 (and_10_out, and_9_out, and_1_out);
  LED X (.in(or_3_out));
  LED Y (.in(and_10_out));
endmodule
