// Logisim project verrou-nor.circ as structural Verilog: 2 circuits, main circuit main
module main (
  input  Set,
  input  Reset,
  output out_3
);

  wire nor_1_out;

  nor nor_1 (nor_1_out, out_3, Set);
  nor nor_2 (out_3, nor_1_out, Reset);
endmodule

module circuit_metastable (
  input  Set,
  output out_2
);

  wire nor_1_out;

  nor nor_1 (nor_1_out, out_2, Set);
  nor nor_2 (out_2, nor_1_out, Set);

  // Notes on the sheet:
  //   Reset
endmodule
